// Digital circuit Accumulator.dig as structural Verilog
module Accumulator (
  input  CLK,
  input  nLA,
  input  [7:0] ABus,
  input  EA,
  output [7:0] QA,
  output [7:0] Qbus
);

  d_flipflop_w_latch_remake d_flipflop_w_latch_remake_1 (.CLR(1'b0), .CLK(CLK), .nL(nLA), .nOE(1'b0), .D(ABus), .Q(QA));
  assign Qbus = EA ? QA : 8'bz;  // Driver driver_1
endmodule
