// Digital circuit Add-Sub.dig as structural Verilog
module Add_Sub (
  input  [7:0] B,
  input  [7:0] A,
  input  Su,
  input  Eu,
  output [7:0] RBus
);

  wire [7:0] add_1_s, multiplexer_1_out, sub_1_s;

  assign RBus = Eu ? multiplexer_1_out : 8'bz;  // Driver driver_1
  Multiplexer #(.Bits(8)) multiplexer_1 (.sel(Su), .in_0(add_1_s), .in_1(sub_1_s), .out(multiplexer_1_out));
  Sub #(.Bits(8)) sub_1 (.a(A), .b(B), .c_i(1'b0), .s(sub_1_s));  // open: c_o
  Add #(.Bits(8)) add_1 (.a(A), .b(B), .c_i(1'b0), .s(add_1_s));  // open: c_o
endmodule
