// Digital circuit B reg.dig as structural Verilog
module B_reg (
  input  CLK,
  input  nLB,
  input  [7:0] BBus,
  output [7:0] QB
);

  d_flipflop_w_latch_remake d_flipflop_w_latch_remake_1 (.CLR(1'b0), .CLK(CLK), .nL(nLB), .nOE(1'b0), .D(BBus), .Q(QB));
endmodule
