// Digital circuit Controller.dig as structural Verilog
module Controller (
  input  Clk,
  input  T3,
  input  CLR,
  input  [3:0] FromIR,
  input  T1,
  output Cp,
  output nLo,
  output nLb,
  output Eu,
  output Su,
  output Ea,
  output nLa,
  output nEi,
  output nLi,
  output nCE,
  output nLm,
  output Ep,
  output [11:0] d
);

  wire or_1_out;
  wire [3:0] ARom_d, counterpreset_1_out;

  or or_1 (or_1_out, T1, CLR);
  ROM #(.AddrBits(4), .Bits(4)) ARom (.A(FromIR), .sel(1'b1), .D(ARom_d));
  CounterPreset #(.Bits(4)) counterpreset_1 (
    .en(1'b1), .C(~Clk), .dir(1'b0), .in(ARom_d), .ld(T3), .clr(or_1_out), .out(counterpreset_1_out));  // open: ovf
  // Probe on ARom_d
  // Probe on counterpreset_1_out
  ROM #(.AddrBits(4), .Bits(12)) CRom (.A(counterpreset_1_out), .sel(1'b1), .D({Cp, d[10:0]}));
  // Probe on {Cp, d[10:0]}

  assign d[11] = Cp;
  assign Ea = d[4];
  assign Ep = d[10];
  assign Eu = d[2];
  assign nCE = d[8];
  assign nEi = d[6];
  assign nLa = d[5];
  assign nLb = d[1];
  assign nLi = d[7];
  assign nLm = d[9];
  assign nLo = d[0];
  assign Su = d[3];

  // Notes on the sheet:
  //   Clk: Hz: 5
  //   contents of ARom (hex, n*v repeats v):
  //   3,6,3e9,11*0,44c
  //   contents of CRom (hex, n*v repeats v):
  //   5e3,be3,263,1a3,2c3,3e3,1a3,2e1,3c7,1a3,2e1,3cf,3f2,3e3,3e3
endmodule
