// Digital circuit Counter.dig as structural Verilog
module Counter (
  input  Cp,
  input  nClr,
  input  Ep,
  input  nCLK,
  output [3:0] Qbus,
  output [3:0] P
);

  Counter #(.Bits(4)) counter_1 (.en(Cp), .C(~nCLK), .clr(~nClr), .out(P));  // open: ovf
  assign Qbus = Ep ? P : 4'bz;  // Driver driver_1

  // Notes on the sheet:
  //   nCLK: Hz: 5
endmodule
