// Digital circuit Instruction Register.dig as structural Verilog
module Instruction_Register (
  input  [7:0] Dbus,
  input  Clr,
  input  nEi,
  input  nLi,
  input  Clk,
  output [3:0] QCon,
  output [3:0] QBus
);

  wire [3:0] d_flipflop_w_latch_remake_1_q;

  d_flipflop_w_latch_remake d_flipflop_w_latch_remake_1 (
    .CLR(Clr), .CLK(Clk), .nL(nLi), .nOE(1'b0), .D(Dbus), .Q({QCon, d_flipflop_w_latch_remake_1_q}));
  assign QBus = ~nEi ? d_flipflop_w_latch_remake_1_q : 4'bz;  // DriverInvSel driverinvsel_1
endmodule
