// Digital circuit MAR.dig as structural Verilog
module MAR (
  input  [3:0] Dbus,
  input  Clk,
  input  nLm,
  output [3:0] QRam
);

  wire d_flipflop_8_bit_1_q4, d_flipflop_8_bit_1_q5, d_flipflop_8_bit_1_q6, d_flipflop_8_bit_1_q7;

  d_flipflop_8_bit d_flipflop_8_bit_1 (
    .CLR(1'b0), .CLK(Clk), .nL(nLm), .nOE(1'b0), .D0(Dbus[0]), .D1(Dbus[1]), .D2(Dbus[2]), .D3(Dbus[3]),
    .D4(1'b0), .D5(1'b0), .D6(1'b0), .D7(1'b0), .Q0(QRam[0]), .Q1(QRam[1]), .Q2(QRam[2]), .Q3(QRam[3]),
    .Q4(d_flipflop_8_bit_1_q4), .Q5(d_flipflop_8_bit_1_q5), .Q6(d_flipflop_8_bit_1_q6),
    .Q7(d_flipflop_8_bit_1_q7));
endmodule
