// Digital circuit Out Reg.dig as structural Verilog
module Out_Reg (
  input  CLK,
  input  nLO,
  input  [7:0] Obus,
  output [7:0] QO
);

  d_flipflop_w_latch_remake d_flipflop_w_latch_remake_1 (.CLR(1'b0), .CLK(CLK), .nL(nLO), .nOE(1'b0), .D(Obus), .Q(QO));
endmodule
