// Digital circuit RAM.dig as structural Verilog
module RAM (
  input  [3:0] fMar,
  input  nCE,
  output [7:0] Qbus
);

  RAMSinglePortSel #(.AddrBits(4), .Bits(8)) ramsingleportsel_1 (.A(fMar), .CS(~nCE), .WE(~1'b1), .OE(~1'b0), .D(Qbus));
endmodule
