// Digital circuit RAM0804.dig as structural Verilog
module RAM0804 (
  input  [3:0] USER,
  input  [3:0] MAR,
  input  nRun_Prog,
  input  Wr,
  input  [7:0] D,
  input  nCE,
  output [7:0] DQ,
  output [7:0] B
);

  wire multiplexer_1_out, or_1_out;
  wire [3:0] multiplexer_2_out;

  Multiplexer multiplexer_1 (.sel(nRun_Prog), .in_0(1'b0), .in_1(Wr), .out(multiplexer_1_out));
  or or_1 (or_1_out, nRun_Prog, nCE);
  assign DQ = multiplexer_1_out ? D : 8'bz;  // Driver driver_1
  Multiplexer #(.Bits(4)) multiplexer_2 (.sel(nRun_Prog), .in_0(MAR), .in_1(USER), .out(multiplexer_2_out));
  // Probe on multiplexer_2_out
  RAMSinglePortSel #(.AddrBits(4), .Bits(8)) ramsingleportsel_1 (
    .A(multiplexer_2_out), .CS(1'b1), .WE(multiplexer_1_out), .OE(~multiplexer_1_out), .D(DQ));
  assign B = ~or_1_out ? DQ : 8'bz;  // DriverInvSel driverinvsel_1
endmodule
