// Digital circuit RAM0809.dig as structural Verilog
module RAM0809 (
  input  [3:0] USER,
  input  [3:0] MAR,
  input  [1:0] Mode,
  input  Wr,
  input  [7:0] D,
  input  nCE,
  input  CLKROM,
  output [7:0] DQ,
  output [7:0] B
);

  wire multiplexer_2_out;
  wire [3:0] counter_1_out, multiplexer_3_out;
  wire [7:0] multiplexer_1_out, rom_1_d;

  Counter #(.Bits(4)) counter_1 (.en(1'b1), .C(CLKROM), .clr(1'b0), .out(counter_1_out));  // open: ovf
  ROM #(.AddrBits(4), .Bits(8)) rom_1 (.A(counter_1_out), .sel(1'b1), .D(rom_1_d));
  Multiplexer #(.Selector_Bits(2), .Bits(8)) multiplexer_1 (
    .sel(Mode), .in_0(8'h1), .in_1(D), .in_2(rom_1_d), .in_3(8'h1), .out(multiplexer_1_out));
  Multiplexer #(.Selector_Bits(2)) multiplexer_2 (
    .sel(Mode), .in_0(1'b0), .in_1(Wr), .in_2(1'b1), .in_3(1'b1), .out(multiplexer_2_out));
  assign DQ = multiplexer_2_out ? multiplexer_1_out : 8'bz;  // Driver driver_1
  Multiplexer #(.Selector_Bits(2), .Bits(4)) multiplexer_3 (
    .sel(Mode), .in_0(MAR), .in_1(USER), .in_2(counter_1_out), .in_3(4'b0001), .out(multiplexer_3_out));
  RAMSinglePortSel #(.AddrBits(4), .Bits(8)) ramsingleportsel_1 (
    .A(multiplexer_3_out), .CS(1'b1), .WE(multiplexer_2_out), .OE(~multiplexer_2_out), .D(DQ));
  assign B = ~nCE ? DQ : 8'bz;  // DriverInvSel driverinvsel_1

  // Notes on the sheet:
  //   CLKROM: Hz: 50000
  //   contents of rom_1 (hex, n*v repeats v):
  //   a,1b,2c,e0,f0,6,7,8,9,a,8,3,2,4,5,3
endmodule
