// Digital circuit SAP-1.dig as structural Verilog
module SAP_1 (
  input  clk,
  input  [7:0] in_2,
  input  [3:0] in_3,
  input  clk_2,
  input  [1:0] Mode,
  input  in_11,
  output [7:0] out_4,
  output out_7,
  output out_8,
  output out_9,
  output out_10,
  output out_12,
  output out_13
);

  wire CLK_t, Cp, Ea, Ep, Eu, HLT, nCE, nCLK, nCLR, nEi, nLa, nLb, nLi, nLm, nLo, Su, Write;
  wire [3:0] counter_1_p, counter_1_qbus, instruction_register_1_qcon, mar_1_qram, out_reg_1_qo;
  wire [7:0] accumulator_1_qa, b_reg_1_qb, ram0809_1_b;
  wire [7:4] out_reg_1_qo_2;
  wire [11:0] controller_1_d;

  nand nand_1 (HLT, instruction_register_1_qcon[3], instruction_register_1_qcon[2], instruction_register_1_qcon[1], instruction_register_1_qcon[0]);
  t_state t_state_1 ();
  RAM0809 ram0809_1 (
    .USER(in_3), .MAR(mar_1_qram), .CLKROM(clk_2), .Mode(Mode), .Wr(Write), .D(in_2), .nCE(nCE), .DQ(out_4),
    .B(ram0809_1_b));
  Controller controller_1 (
    .Clk(CLK_t), .T3(out_13), .T1(out_12), .CLR(in_11), .FromIR(instruction_register_1_qcon), .Cp(Cp),
    .Ep(Ep), .nLm(nLm), .nCE(nCE), .nLi(nLi), .nEi(nEi), .nLa(nLa), .Ea(Ea), .Su(Su), .Eu(Eu), .nLb(nLb),
    .nLo(nLo), .d(controller_1_d));
  Counter counter_1 (.Cp(Cp), .Ep(Ep), .nCLK(nCLK), .nClr(nCLR), .Qbus(counter_1_qbus), .P(counter_1_p));
  MAR mar_1 (.QRam(mar_1_qram), .Dbus(counter_1_qbus), .Clk(CLK_t), .nLm(nLm));
  Instruction_Register instruction_register_1 (
    .QCon(instruction_register_1_qcon), .Dbus(ram0809_1_b), .QBus(counter_1_qbus), .nLi(nLi), .nEi(nEi),
    .Clr(in_11), .Clk(CLK_t));
  // Probe on counter_1_p
  // Probe on mar_1_qram
  // Probe on ram0809_1_b
  // Probe on controller_1_d
  Button button_1 (.out(Write));
  Add_Sub add_sub_1 (.B(b_reg_1_qb), .A(accumulator_1_qa), .RBus(ram0809_1_b), .Su(Su), .Eu(Eu));
  B_reg b_reg_1 (.nLB(nLb), .CLK(CLK_t), .BBus(ram0809_1_b), .QB(b_reg_1_qb));
  Out_Reg out_reg_1 (.nLO(nLo), .CLK(CLK_t), .Obus(ram0809_1_b), .QO({out_reg_1_qo_2, out_reg_1_qo}));
  Accumulator accumulator_1 (
    .nLA(nLa), .CLK(CLK_t), .EA(Ea), .ABus(ram0809_1_b), .Qbus(ram0809_1_b), .QA(accumulator_1_qa));
  and and_1 (CLK_t, clk, HLT);
  not not_1 (nCLR, in_11);
  // Probe on accumulator_1_qa
  // Probe on b_reg_1_qb
  not not_2 (nCLK, CLK_t);
  Seven_Seg_Hex seven_seg_hex_1 (.d(out_reg_1_qo_2), .dp(1'b0));
  Seven_Seg_Hex seven_seg_hex_2 (.d(out_reg_1_qo), .dp(1'b0));

  // Other names for the same wires on the sheet: CLR = in_11; T1 = out_12; T3 = out_13; UserAddr[3:0] = in_3;
  //   UserData[7:0] = in_2

  // Notes on the sheet:
  //   clk_2: Hz: 50000
  //   Mode: default 2
endmodule
