// Digital circuit t-state.dig as structural Verilog
module t_state (
  input  CLR,
  input  CLK,
  output T1,
  output T2,
  output T3,
  output T4,
  output T5,
  output T6
);

  D_FF_AS d_ff_as_1 (.Set(CLR), .D(T6), .C(CLK), .Clr(1'b0), .Q(T1));  // open: nQ
  D_FF_AS d_ff_as_2 (.Set(1'b0), .D(T1), .C(CLK), .Clr(CLR), .Q(T2));  // open: nQ
  D_FF_AS d_ff_as_3 (.Set(1'b0), .D(T2), .C(CLK), .Clr(CLR), .Q(T3));  // open: nQ
  D_FF_AS d_ff_as_4 (.Set(1'b0), .D(T3), .C(CLK), .Clr(CLR), .Q(T4));  // open: nQ
  D_FF_AS d_ff_as_5 (.Set(1'b0), .D(T4), .C(CLK), .Clr(CLR), .Q(T5));  // open: nQ
  D_FF_AS d_ff_as_6 (.Set(1'b0), .D(T5), .C(CLK), .Clr(CLR), .Q(T6));  // open: nQ

  // Notes on the sheet:
  //   CLK: Hz: 5
endmodule
