// Digital circuit ALU-FLAGS.dig as structural Verilog
module ALU_FLAGS (
  input  [7:0] A,
  input  [7:0] T,
  input  [3:0] Selector,
  input  EAlu,
  input  nUF,
  input  Clr,
  input  Clk,
  output Zero_Flag,
  output Sign_Flag,
  output [7:0] Q,
  output [7:0] Qp
);

  wire [7:0] ADD_s, and_1_out, d_flipflop_w_latch_remake_1_q, DECREMENT_2_s, DECREMENT_s, INCREMENT_2_s,
       INCREMENT_s, not_1_out, or_1_out, RAL_out, RAR_out, SUB_s, xor_1_out;

  d_flipflop_w_latch_remake d_flipflop_w_latch_remake_1 (
    .CLR(Clr), .CLK(Clk), .nL(nUF), .nOE(1'b0), .D(A), .Q(d_flipflop_w_latch_remake_1_q));
  Add #(.Bits(8)) ADD (.a(A), .b(T), .c_i(1'b0), .s(ADD_s));  // open: c_o
  Sub #(.Bits(8)) SUB (.a(A), .b(T), .c_i(1'b0), .s(SUB_s));  // open: c_o
  Add #(.Bits(8)) INCREMENT (.a(A), .b(8'h1), .c_i(1'b0), .s(INCREMENT_s));  // open: c_o
  Sub #(.Bits(8)) DECREMENT (.a(A), .b(8'h1), .c_i(1'b0), .s(DECREMENT_s));  // open: c_o
  BarrelShifter #(.Bits(8), .barrelShifterMode("rotate")) RAL (.in(A), .shift(4'b0001), .out(RAL_out));
  BarrelShifter #(.Bits(8), .barrelShifterMode("rotate"), .direction("right")) RAR (
    .in(A), .shift(4'b0001), .out(RAR_out));
  assign and_1_out = A & T;  // And and_1, 8 bits wide
  assign or_1_out = A | T;  // Or or_1, 8 bits wide
  assign xor_1_out = A ^ T;  // XOr xor_1, 8 bits wide
  assign not_1_out = ~A;  // Not not_1, 8 bits wide
  Add #(.Bits(8)) INCREMENT_2 (.a(T), .b(8'h1), .c_i(1'b0), .s(INCREMENT_2_s));  // open: c_o
  Sub #(.Bits(8)) DECREMENT_2 (.a(T), .b(8'h1), .c_i(1'b0), .s(DECREMENT_2_s));  // open: c_o
  Comparator #(.Signed("true"), .Bits(8)) FLAGS (
    .a(d_flipflop_w_latch_remake_1_q), .b({8{1'b0}}), .eq(Zero_Flag), .lt(Sign_Flag));  // open: gt
  Multiplexer #(.Selector_Bits(4), .Bits(8)) multiplexer_1 (
    .sel(Selector), .in_0(ADD_s), .in_1(SUB_s), .in_2(INCREMENT_s), .in_3(DECREMENT_s), .in_4(RAL_out),
    .in_5(RAR_out), .in_6(and_1_out), .in_7(or_1_out), .in_8(xor_1_out), .in_9(not_1_out),
    .in_10(INCREMENT_2_s), .in_11(DECREMENT_2_s), .in_12({8{1'b0}}), .in_13({8{1'b0}}), .in_14({8{1'b0}}),
    .in_15({8{1'b0}}), .out(Qp));
  assign Q = EAlu ? Qp : 8'bz;  // Driver driver_1

  // Notes on the sheet:
  //   nUF: Update the Flags
  //   ANA
  //   ORA
  //   XRA
  //   CMA
  //   0 - ADD
  //   1 - SUB
  //   2 - INR A
  //   3 - DCR A
  //   4 - RAL
  //   5 - RAR
  //   6 - ANA
  //   7 - ORA
  //   9 - XRA
  //   10 - CMA
  //   11 - DCR T
  //   12 - INR T
endmodule
