// Digital circuit Accumulator.dig as structural Verilog
module Accumulator (
  input  CLK,
  input  nLA,
  input  [7:0] ABus,
  input  nEA,
  input  CLR,
  output [7:0] QA,
  output [7:0] Qbus,
  output [7:0] QAp
);

  d_flipflop_w_latch_remake d_flipflop_w_latch_remake_1 (.CLR(CLR), .CLK(CLK), .nL(nLA), .nOE(1'b0), .D(ABus), .Q(QA));
  assign Qbus = ~nEA ? QA : 8'bz;  // DriverInvSel driverinvsel_1

  assign QAp = QA;
endmodule
