// Digital circuit C reg.dig as structural Verilog
module C_reg (
  input  CLK,
  input  nLC,
  input  [7:0] CBus,
  input  nEC,
  output [7:0] QC,
  output [7:0] QCp
);

  assign QC = ~nEC ? QCp : 8'bz;  // DriverInvSel driverinvsel_1
  d_flipflop_w_latch_remake d_flipflop_w_latch_remake_1 (
    .CLR(1'b0), .CLK(CLK), .nL(nLC), .nOE(1'b0), .D(CBus), .Q(QCp));
endmodule
