// Digital circuit Controller.dig as structural Verilog
module Controller (
  input  Clk,
  input  T3,
  input  CLR,
  input  [7:0] IR,
  input  T1,
  output [31:0] CON
);

  wire or_1_out;
  wire [7:0] ARom_d, counterpreset_1_out;

  or or_1 (or_1_out, T1, CLR);
  ROM #(.AddrBits(8), .isProgramMemory("true"), .Bits(8)) ARom (.A(IR), .sel(1'b1), .D(ARom_d));
  CounterPreset #(.Bits(8)) counterpreset_1 (
    .en(1'b1), .C(~Clk), .dir(1'b0), .in(ARom_d), .ld(T3), .clr(or_1_out), .out(counterpreset_1_out));  // open: ovf
  // Probe on ARom_d
  // Probe on counterpreset_1_out
  ROM #(.AddrBits(8), .isProgramMemory("true"), .Bits(32)) CRom (.A(counterpreset_1_out), .sel(1'b1), .D(CON));

  // Notes on the sheet:
  //   Clk: Hz: 5
  //   contents of ARom (hex, n*v repeats v):
  //   3,4*0,13,7,6*0,15,a,46*0,11,4,65*0,d,f
  //   contents of CRom (hex, n*v repeats v):
  //   1ab07ff,1db07ff,19903ff,39b07ff,1ab07ff,1db07ff,39907fd,1ab07ff
  //   ,1db07ff,39907ef,1ab07ff,1db07ff,39907bf,19b07db,39a87fd,19b077b
  //   ,39a87fd,19b07fa,39a9ffd,19b07db,39bdfef,19b077b,39bdfbf
endmodule
