// Digital circuit Generator.dig as structural Verilog
module Generator (
  input  Cin,
  input  RESET,
  input  St,
  input  nA_M,
  input  nHlt,
  output CLR,
  output nCLR,
  output nCLK,
  output CLK
);

  wire multiplexer_1_out;

  Multiplexer multiplexer_1 (.sel(nA_M), .in_0(Cin), .in_1(St), .out(multiplexer_1_out));
  RS_FF_AS rs_ff_as_1 (.S(Cin), .R(RESET), .nQ(CLR));  // open: Q
  and and_1 (CLK, multiplexer_1_out, nHlt);
  not not_1 (nCLR, CLR);
  not not_2 (nCLK, CLK);
endmodule
