// Digital circuit IR.dig as structural Verilog
module IR (
  input  Clr,
  input  Clk,
  input  nLi,
  input  [7:0] D,
  output [7:0] Qc
);

  d_flipflop_8_bit d_flipflop_8_bit_1 (
    .D0(D[0]), .D1(D[1]), .D2(D[2]), .D3(D[3]), .D4(D[4]), .D5(D[5]), .D6(D[6]), .D7(D[7]), .nL(nLi),
    .CLK(Clk), .CLR(Clr), .nOE(Clr), .Q0(Qc[0]), .Q1(Qc[1]), .Q2(Qc[2]), .Q3(Qc[3]), .Q4(Qc[4]), .Q5(Qc[5]),
    .Q6(Qc[6]), .Q7(Qc[7]));
endmodule
