// Digital circuit Input Port 1.dig as structural Verilog
module Input_Port_1 (
  input  Clk,
  input  nLI1,
  input  [7:0] HexKey,
  input  nEinput1,
  output [7:0] Q
);

  d_flipflop_w_latch_remake d_flipflop_w_latch_remake_1 (
    .CLR(1'b0), .CLK(Clk), .nL(nLI1), .nOE(nEinput1), .D(HexKey), .Q(Q));
endmodule
