// Digital circuit Input Port 2.dig as structural Verilog
module Input_Port_2 (
  input  Clk,
  input  nEinput2,
  input  Ready,
  input  Serial_Input,
  input  nLI2,
  input  [5:0] DE2,
  output [7:0] Q
);

  d_flipflop_8_bit d_flipflop_8_bit_1 (
    .D0(Ready), .D1(DE2[0]), .D2(DE2[1]), .D3(DE2[2]), .D4(DE2[3]), .D5(DE2[4]), .D6(DE2[5]),
    .D7(Serial_Input), .nL(nLI2), .CLK(Clk), .CLR(1'b0), .nOE(nEinput2), .Q0(Q[0]), .Q1(Q[1]), .Q2(Q[2]),
    .Q3(Q[3]), .Q4(Q[4]), .Q5(Q[5]), .Q6(Q[6]), .Q7(Q[7]));
  // Pins of 1 and 8 bits meet at Q
endmodule
