// Digital circuit Latch 8-bit.dig as structural Verilog
module Latch_8_bit (
  input  [7:0] D,
  input  E,
  output [7:0] Q
);

  Latch latch_1 (.E(E), .D(D[0]), .Q(Q[0]));
  Latch latch_2 (.E(E), .D(D[1]), .Q(Q[1]));
  Latch latch_3 (.E(E), .D(D[2]), .Q(Q[2]));
  Latch latch_4 (.E(E), .D(D[3]), .Q(Q[3]));
  Latch latch_5 (.E(E), .D(D[4]), .Q(Q[4]));
  Latch latch_6 (.E(E), .D(D[5]), .Q(Q[5]));
  Latch latch_7 (.E(E), .D(D[6]), .Q(Q[6]));
  Latch latch_8 (.E(E), .D(D[7]), .Q(Q[7]));
endmodule
