// Digital circuit Latch.dig as structural Verilog
module Latch (
  input  E,
  input  D,
  output Q
);

  wire and_1_out, and_2_out;

  and and_1 (and_1_out, E, D);
  and and_2 (and_2_out, E, ~D);  // And
  RS_FF_AS rs_ff_as_1 (.S(and_1_out), .R(and_2_out), .Q(Q));  // open: nQ
endmodule
