// Digital circuit MAR.dig as structural Verilog
module MAR (
  input  [15:0] Dbus,
  input  Clk,
  input  nLm,
  input  Clr,
  output [15:0] QRam
);

  d_flipflop_16_bit d_flipflop_16_bit_1 (
    .D0(Dbus[0]), .D1(Dbus[1]), .D2(Dbus[2]), .D3(Dbus[3]), .D4(Dbus[4]), .D5(Dbus[5]), .D6(Dbus[6]),
    .D7(Dbus[7]), .D8(Dbus[8]), .D9(Dbus[9]), .D10(Dbus[10]), .D11(Dbus[11]), .D12(Dbus[12]), .D13(Dbus[13]),
    .D14(Dbus[14]), .D15(Dbus[15]), .nL(nLm), .CLK(Clk), .CLR(Clr), .nOE(1'b0), .Q0(QRam[0]), .Q1(QRam[1]),
    .Q2(QRam[2]), .Q3(QRam[3]), .Q4(QRam[4]), .Q5(QRam[5]), .Q6(QRam[6]), .Q7(QRam[7]), .Q8(QRam[8]),
    .Q9(QRam[9]), .Q10(QRam[10]), .Q11(QRam[11]), .Q12(QRam[12]), .Q13(QRam[13]), .Q14(QRam[14]),
    .Q15(QRam[15]));
  // Pins of 4 and 16 bits meet at QRam
  // Pins of 4 and 16 bits meet at Dbus
endmodule
