// Digital circuit MDR.dig as structural Verilog
module MDR (
  input  Clk,
  input  nLmdr,
  input  [7:0] DBs,
  input  Dir,
  input  nEmdr,
  input  [7:0] fRAM,
  output [7:0] tRAM,
  output [7:0] QBs
);

  d_flipflop_w_latch_remake to_BUS (.D(fRAM), .nL(Dir), .CLK(Clk), .CLR(1'b0), .nOE(nEmdr), .Q(QBs));
  d_flipflop_w_latch_remake to_RAM (.D(DBs), .nL(nLmdr), .CLK(Clk), .CLR(1'b0), .nOE(Dir), .Q(tRAM));
endmodule
