// Digital circuit Output Port 3.dig as structural Verilog
module Output_Port_3 (
  input  [7:0] DBs,
  input  Clk,
  input  nLout3,
  input  Clr,
  output [7:0] Qout3
);

  d_flipflop_w_latch_remake d_flipflop_w_latch_remake_1 (
    .CLR(Clr), .CLK(Clk), .nL(nLout3), .nOE(1'b0), .D(DBs), .Q(Qout3));
  // Pins of 1 and 8 bits meet at DBs
endmodule
