// Digital circuit Output Port 4.dig as structural Verilog
module Output_Port_4 (
  input  Clk,
  input  nLout4,
  input  [7:0] DBs,
  input  Clr,
  output [7:0] Qout4,
  output SerialOut,
  output Acknowledge
);

  d_flipflop_8_bit d_flipflop_8_bit_1 (
    .CLR(Clr), .CLK(Clk), .nL(nLout4), .nOE(1'b0), .D0(DBs[0]), .D1(DBs[1]), .D2(DBs[2]), .D3(DBs[3]),
    .D4(DBs[4]), .D5(DBs[5]), .D6(DBs[6]), .D7(DBs[7]), .Q0(Qout4[0]), .Q1(Qout4[1]), .Q2(Qout4[2]),
    .Q3(Qout4[3]), .Q4(Qout4[4]), .Q5(Qout4[5]), .Q6(Qout4[6]), .Q7(Acknowledge));
  // Pins of 1 and 8 bits meet at {Acknowledge, Qout4[6:0]}

  assign Qout4[7] = Acknowledge;
  assign SerialOut = Qout4[0];
endmodule
