// Digital circuit PC-Sap1.dig as structural Verilog
module PC_Sap1 (
  input  Cp,
  input  nClr,
  input  Ep,
  input  nCLK,
  output [15:0] Qbus,
  output [15:0] P
);

  Counter #(.Bits(16)) counter_1 (.en(Cp), .C(~nCLK), .clr(~nClr), .out(P));  // open: ovf
  assign Qbus = Ep ? P : 16'bz;  // Driver driver_1

  // Notes on the sheet:
  //   nCLK: Hz: 5
endmodule
