// Digital circuit PC.dig as structural Verilog
module PC (
  input  Ep,
  input  Cp,
  input  nCLK,
  input  nLd,
  input  nClr,
  input  [7:0] Ain,
  input  Asel,
  input  LAin,
  input  PCsel,
  output [15:0] Qp,
  output [15:0] Q,
  output [7:0] Qbus
);

  wire demultiplexer_1_out_0, demultiplexer_1_out_1;
  wire [7:0] latch_8_bit_1_q, latch_8_bit_2_q, multiplexer_1_out;

  Demultiplexer demultiplexer_1 (.sel(Asel), .in(LAin), .out_0(demultiplexer_1_out_0), .out_1(demultiplexer_1_out_1));
  Latch_8_bit latch_8_bit_1 (.D(Ain), .E(demultiplexer_1_out_0), .Q(latch_8_bit_1_q));
  Latch_8_bit latch_8_bit_2 (.D(Ain), .E(demultiplexer_1_out_1), .Q(latch_8_bit_2_q));
  CounterPreset #(.Bits(16)) counterpreset_1 (
    .en(Cp), .C(~nCLK), .dir(1'b0), .in({latch_8_bit_2_q, latch_8_bit_1_q}), .ld(nLd), .clr(~nClr), .out(Qp));  // open: ovf
  assign Q = Ep ? Qp : 16'bz;  // Driver driver_1
  Multiplexer #(.Bits(8)) multiplexer_1 (.sel(PCsel), .in_0(Q[7:0]), .in_1(Q[15:8]), .out(multiplexer_1_out));
  assign Qbus = Ep ? multiplexer_1_out : 8'bz;  // Driver driver_2

  // Notes on the sheet:
  //   nCLK: Hz: 5
  //   Ain: load address to PC
endmodule
