// Digital circuit RAM-ROM.dig as structural Verilog
module RAM_ROM (
  input  ClkP,
  input  [15:0] fMAR,
  input  [7:0] fMDR,
  input  nRUN_Prog,
  input  [15:0] As,
  input  [15:0] Ae,
  input  Write,
  input  DiR,
  output nEoa,
  output [7:0] tMDR
);

  wire comparator_1_eq, multiplexer_1_out, multiplexer_3_out, not_2_out;
  wire [7:0] driver_1_out, rom_1_d;
  wire [15:0] counterpreset_1_out, multiplexer_2_out;

  CounterPreset #(.Bits(16)) counterpreset_1 (
    .en(nEoa), .C(ClkP), .dir(1'b0), .in(As), .ld(Write), .clr(1'b0), .out(counterpreset_1_out));  // open: ovf
  // Probe on counterpreset_1_out
  Comparator #(.Bits(16)) comparator_1 (.a(Ae), .b(counterpreset_1_out), .eq(comparator_1_eq));  // open: gt, lt
  not not_1 (nEoa, comparator_1_eq);
  // Probe on counterpreset_1_out
  ROM #(.AddrBits(16), .isProgramMemory("true"), .Bits(8)) rom_1 (.A(counterpreset_1_out), .sel(1'b1), .D(rom_1_d));
  Multiplexer multiplexer_1 (.sel(nRUN_Prog), .in_0(DiR), .in_1(1'b1), .out(multiplexer_1_out));
  assign driver_1_out = nRUN_Prog ? rom_1_d : 8'bz;  // Driver driver_1
  Multiplexer #(.Bits(16)) multiplexer_2 (
    .sel(nRUN_Prog), .in_0(fMAR), .in_1(counterpreset_1_out), .out(multiplexer_2_out));
  not not_2 (not_2_out, multiplexer_1_out);
  RAMSinglePortSel #(.AddrBits(16), .Bits(8)) ramsingleportsel_1 (
    .A(multiplexer_2_out), .CS(1'b1), .WE(multiplexer_1_out), .OE(not_2_out), .D(driver_1_out));
  Multiplexer multiplexer_3 (.sel(nRUN_Prog), .in_0(DiR), .in_1(1'b0), .out(multiplexer_3_out));
  assign driver_1_out = multiplexer_3_out ? fMDR : 8'bz;  // Driver driver_2
  assign tMDR = ~multiplexer_3_out ? driver_1_out : 8'bz;  // DriverInvSel driverinvsel_1

  // Other names for the same wires on the sheet: EndAddr[15:0] = Ae; Eoa = nEoa; Lr = DiR; Mode = nRUN_Prog;
  //   StartAddr[15:0] = As

  // Notes on the sheet:
  //   ClkP: Hz: 2
  //   nRUN_Prog: default 1
  //   Ae: default 12
  //   contents of rom_1 (hex, n*v repeats v):
  //   3e,22,6,21,e,20,80,81,3d,5,d
endmodule
