// Digital circuit SAP2.dig as structural Verilog
module SAP2 (
  input  Serial_Input,
  input  clk,
  input  in_4,
  input  in_5,
  input  [15:0] in_9,
  input  [15:0] in_10,
  input  clk_2,
  input  [5:0] DE2,
  input  in_18,
  output Serial_Output,
  output out_6,
  output out_7,
  output out_8,
  output [7:0] out_12,
  output out_13,
  output out_14,
  output [7:0] Output_4,
  output [7:0] Output_3
);

  wire Ack, Asel, Clk_t, Clr, keyboard_1_av, mar_1_p4, Mode, nClk, nClr, or_1_out, or_2_out, pc_1_p9,
       pc_1_p12, reset_t, St;
  wire [7:0] accumulator_1_qa, Alup, AReg, BReg, CReg, input_port_1_1_q, ir_1_qc, RAM_ROM_p7, RAM_ROM_p9,
       temp_1_qt, TReg;
  wire [15:0] keyboard_1_d;
  wire [31:0] Controller;

  or or_1 (or_1_out, Clr, Controller[25]);
  Generator Clock_Generator (
    .Cin(clk), .RESET(in_18), .St(St), .nA_M(in_4), .nCLR(nClr), .CLR(Clr), .nCLK(nClk), .CLK(Clk_t),
    .nHlt(in_5));
  T_Counter t_counter_1 (.Clk(Clk_t), .Clr(or_1_out), .Q(out_12), .T1(out_6), .T3(out_7), .T4(out_8));
  Keyboard keyboard_1 (.C(Clk_t), .en(Ack), .D(keyboard_1_d), .av(keyboard_1_av));
  or or_2 (or_2_out, Clk_t, Clr);
  Input_Port_1 input_port_1_1 (
    .Clk(Clk_t), .nLI1(Controller[24]), .HexKey(keyboard_1_d[7:0]), .nEinput1(1'b1), .Q(input_port_1_1_q));
  Input_Port_2 input_port_2_1 (
    .Ready(keyboard_1_av), .DE2(DE2), .Serial_Input(Serial_Input), .nLI2(Controller[23]), .Clk(Clk_t),
    .nEinput2(1'b1), .Q(input_port_1_1_q[0]));
  // PC pc_1: pin names not known; wires that end beside it: Controller[26], Controller[21], Controller[22], nClk, Controller[27], Asel, Controller[29], nClr, pc_1_p9, input_port_1_1_q, input_port_1_1_q, pc_1_p12
  // MAR mar_1: pin names not known; wires that end beside it: Controller[20], Clk_t, Clr, mar_1_p4, pc_1_p9
  // RAM_ROM RAM_ROM: pin names not known; wires that end beside it: Mode, in_9, in_10, Clr, clk_2, Controller[18], RAM_ROM_p7, mar_1_p4, RAM_ROM_p9, Mode
  MDR mdr_1 (
    .nLmdr(Controller[19]), .Dir(Controller[18]), .Clk(Clk_t), .nEmdr(Controller[17]),
    .DBs(input_port_1_1_q), .QBs(input_port_1_1_q), .tRAM(RAM_ROM_p7), .fRAM(RAM_ROM_p9));
  Controller controller_1 (
    .Clk(or_2_out), .T3(out_7), .T1(out_6), .CLR(Clr), .IR(ir_1_qc),
    .CON({Controller[31:29], Asel, Controller[27:0]}));
  IR ir_1 (.nLi(Controller[10]), .Clk(Clk_t), .Clr(Clr), .D(input_port_1_1_q), .Qc(ir_1_qc));
  // Probe on mar_1_p4
  // Probe on ir_1_qc
  // Probe on pc_1_p12
  // Probe on {Controller[31:29], Asel, Controller[27:0]}
  // Probe on Alup
  ALU_FLAGS alu_flags_1 (
    .A(accumulator_1_qa), .T(TReg), .Zero_Flag(out_13), .Sign_Flag(out_14), .Selector(Controller[14:11]),
    .EAlu(Controller[15]), .Clr(Clr), .nUF(Controller[16]), .Clk(Clk_t), .Qp(Alup), .Q(input_port_1_1_q));
  // Probe on {Controller[31:29], Asel, Controller[27:0]}
  Accumulator accumulator_1 (
    .nLA(Controller[1]), .nEA(Controller[0]), .CLK(Clk_t), .CLR(Clr), .ABus(input_port_1_1_q),
    .Qbus(input_port_1_1_q), .QA(accumulator_1_qa), .QAp(AReg));
  Temp temp_1 (
    .nEt(Controller[3]), .nLT(Controller[2]), .CLK(Clk_t), .QB(input_port_1_1_q), .TBus(input_port_1_1_q),
    .QT(temp_1_qt), .QTp(TReg));
  B_reg b_reg_1 (
    .nEB(Controller[5]), .nLB(Controller[4]), .CLK(Clk_t), .QB(input_port_1_1_q), .BBus(input_port_1_1_q),
    .QBp(BReg));
  C_reg c_reg_1 (
    .nEC(Controller[7]), .nLC(Controller[6]), .CLK(Clk_t), .QC(input_port_1_1_q), .CBus(input_port_1_1_q),
    .QCp(CReg));
  Output_Port_3 output_port_3_1 (
    .nLout3(Controller[8]), .Clr(Clr), .Clk(Clk_t), .Qout3(Output_3), .DBs(input_port_1_1_q[0]));
  // Output_Port_4 output_port_4_1: pin names not known; wires that end beside it: input_port_1_1_q, Controller[9], Serial_Output, Clr, Output_4, Clk_t, Ack
  Button STEP (.out(St));
  // Probe on temp_1_qt
  // Probe on AReg
  // Probe on accumulator_1_qa
  // Probe on BReg
  // Probe on CReg
  // Probe on TReg
  // Probe on AReg
  // Probe on TReg
  // Probe on BReg
  // Probe on CReg
  // Probe on Alup
  Button button_1 (.out(reset_t));
  // Pins of 1 and 8 bits meet at input_port_1_1_q

  // Other names for the same wires on the sheet: ClkP = clk_2; nEA = Controller[0]; nLA = Controller[1];
  //   nLT = Controller[2]; nET = Controller[3]; nLB = Controller[4]; nEB = Controller[5]; nLC = Controller[6];
  //   nEC = Controller[7]; nLO3 = Controller[8]; nLO4 = Controller[9]; nLI = Controller[10];
  //   SEL[3:0] = Controller[14:11]; EAlu = Controller[15]; nUF = Controller[16]; nEMDR = Controller[17];
  //   DIR = Controller[18]; nLMDR = Controller[19]; nLM = Controller[20]; EP = Controller[21]; CP = Controller[22];
  //   nLI2 = Controller[23]; nLI1 = Controller[24]; TReset = Controller[25]; PCsel = Controller[26];
  //   LAin = Controller[27]; Controller[28] = Asel; nLd = Controller[29]; EndAddr[15:0] = in_10; nA_M = in_4;
  //   nEoA = Mode; nhlt = in_5; Reset = in_18; Sflag = out_14; StartAddr[15:0] = in_9; T1 = out_6; T3 = out_7;
  //   T4 = out_8; Write = Clr; ZFlag = out_13

  // Notes on the sheet:
  //   clk: Hz: 5
  //   in_4: default 1
  //   in_5: default 1
  //   in_10: default 41216
  //   clk_2: Hz: 2147483647
  //   PC
  //   InP
  //   MAR
  //   MDR
  //   ALU
  //   Out
  //   IR
  //   C
  //   T
  //   B
  //   A
  //   CONTROLS
  //   ~AUTO/MANUAL
  //   RESET
  //   ~HALT
  //   Registers and ALU
  //   Flags
  //   Zero
  //   Sign
  //   T-States
  //   T1
  //   T3
  //   T4
  //   RAM PROGRAM
  //   START ADDRESS
  //   END ADDRESS
  //   REPROGRAM
endmodule
