// Digital circuit T-Counter.dig as structural Verilog
module T_Counter (
  input  Clk,
  input  Clr,
  output [7:0] Q,
  output T1,
  output T3,
  output T4
);

  Counter #(.Bits(8)) counter_1 (.en(1'b1), .C(Clk), .clr(Clr), .out(Q));  // open: ovf
  Comparator #(.Bits(8)) comparator_1 (.a(Q), .b({8{1'b0}}), .eq(T1));  // open: gt, lt
  Comparator #(.Bits(8)) comparator_2 (.a(Q), .b(8'h3), .eq(T3));  // open: gt, lt
  Comparator #(.Bits(8)) comparator_3 (.a(Q), .b(8'h4), .eq(T4));  // open: gt, lt
endmodule
