// Digital circuit Temp.dig as structural Verilog
module Temp (
  input  CLK,
  input  nLT,
  input  [7:0] TBus,
  input  nEt,
  output [7:0] QB,
  output [7:0] QT,
  output [7:0] QTp
);

  assign QB = ~nEt ? QTp : 8'bz;  // DriverInvSel driverinvsel_1
  d_flipflop_w_latch_remake d_flipflop_w_latch_remake_1 (
    .CLR(1'b0), .CLK(CLK), .nL(nLT), .nOE(1'b0), .D(TBus), .Q(QTp));

  assign QT = QB;
endmodule
