// Digital circuit d flipflop 16 bit.dig as structural Verilog
module d_flipflop_16_bit (
  input  CLR,
  input  CLK,
  input  nL,
  input  nOE,
  input  D0,
  input  D1,
  input  D2,
  input  D3,
  input  D4,
  input  D5,
  input  D6,
  input  D7,
  input  D8,
  input  D9,
  input  D10,
  input  D11,
  input  D12,
  input  D13,
  input  D14,
  input  D15,
  output Q0,
  output Q1,
  output Q2,
  output Q3,
  output Q4,
  output Q5,
  output Q6,
  output Q7,
  output Q8,
  output Q9,
  output Q10,
  output Q11,
  output Q12,
  output Q13,
  output Q14,
  output Q15
);

  wire and_1_out, and_2_out, and_3_out, and_4_out, and_5_out, and_6_out, and_7_out, and_8_out, and_9_out,
       and_10_out, and_11_out, and_12_out, and_13_out, and_14_out, and_15_out, and_16_out, and_17_out,
       and_18_out, and_19_out, and_20_out, and_21_out, and_22_out, and_23_out, and_24_out, and_25_out,
       and_26_out, and_27_out, and_28_out, and_29_out, and_30_out, and_31_out, and_32_out, d_ff_as_1_q,
       d_ff_as_2_q, d_ff_as_3_q, d_ff_as_4_q, d_ff_as_5_q, d_ff_as_6_q, d_ff_as_7_q, d_ff_as_8_q,
       d_ff_as_9_q, d_ff_as_10_q, d_ff_as_11_q, d_ff_as_12_q, d_ff_as_13_q, d_ff_as_14_q, d_ff_as_15_q,
       d_ff_as_16_q, nor_1_out, not_1_out, or_1_out, or_2_out, or_3_out, or_4_out, or_5_out, or_6_out,
       or_7_out, or_8_out, or_9_out, or_10_out, or_11_out, or_12_out, or_13_out, or_14_out, or_15_out,
       or_16_out, or_17_out;

  or or_1 (or_1_out, nL, nL);
  nor nor_1 (nor_1_out, nOE, nOE);
  not not_1 (not_1_out, or_1_out);
  and and_1 (and_1_out, d_ff_as_1_q, or_1_out);
  and and_2 (and_2_out, D0, not_1_out);
  and and_3 (and_3_out, d_ff_as_2_q, or_1_out);
  and and_4 (and_4_out, D1, not_1_out);
  and and_5 (and_5_out, d_ff_as_3_q, or_1_out);
  and and_6 (and_6_out, D2, not_1_out);
  and and_7 (and_7_out, d_ff_as_4_q, or_1_out);
  and and_8 (and_8_out, D3, not_1_out);
  and and_9 (and_9_out, d_ff_as_5_q, or_1_out);
  and and_10 (and_10_out, D4, not_1_out);
  and and_11 (and_11_out, d_ff_as_6_q, or_1_out);
  and and_12 (and_12_out, D5, not_1_out);
  and and_13 (and_13_out, d_ff_as_7_q, or_1_out);
  and and_14 (and_14_out, D6, not_1_out);
  and and_15 (and_15_out, d_ff_as_8_q, or_1_out);
  and and_16 (and_16_out, D7, not_1_out);
  and and_17 (and_17_out, d_ff_as_9_q, or_1_out);
  and and_18 (and_18_out, D8, not_1_out);
  and and_19 (and_19_out, d_ff_as_10_q, or_1_out);
  and and_20 (and_20_out, D9, not_1_out);
  and and_21 (and_21_out, d_ff_as_11_q, or_1_out);
  and and_22 (and_22_out, D10, not_1_out);
  and and_23 (and_23_out, d_ff_as_12_q, or_1_out);
  and and_24 (and_24_out, D11, not_1_out);
  and and_25 (and_25_out, d_ff_as_13_q, or_1_out);
  and and_26 (and_26_out, D12, not_1_out);
  and and_27 (and_27_out, d_ff_as_14_q, or_1_out);
  and and_28 (and_28_out, D13, not_1_out);
  and and_29 (and_29_out, d_ff_as_15_q, or_1_out);
  and and_30 (and_30_out, D14, not_1_out);
  and and_31 (and_31_out, d_ff_as_16_q, or_1_out);
  and and_32 (and_32_out, D15, not_1_out);
  or or_2 (or_2_out, and_1_out, and_2_out);
  or or_3 (or_3_out, and_3_out, and_4_out);
  or or_4 (or_4_out, and_5_out, and_6_out);
  or or_5 (or_5_out, and_7_out, and_8_out);
  or or_6 (or_6_out, and_9_out, and_10_out);
  or or_7 (or_7_out, and_11_out, and_12_out);
  or or_8 (or_8_out, and_13_out, and_14_out);
  or or_9 (or_9_out, and_15_out, and_16_out);
  or or_10 (or_10_out, and_17_out, and_18_out);
  or or_11 (or_11_out, and_19_out, and_20_out);
  or or_12 (or_12_out, and_21_out, and_22_out);
  or or_13 (or_13_out, and_23_out, and_24_out);
  or or_14 (or_14_out, and_25_out, and_26_out);
  or or_15 (or_15_out, and_27_out, and_28_out);
  or or_16 (or_16_out, and_29_out, and_30_out);
  or or_17 (or_17_out, and_31_out, and_32_out);
  D_FF_AS d_ff_as_1 (.Set(1'b0), .D(or_2_out), .C(CLK), .Clr(CLR), .Q(d_ff_as_1_q));  // open: nQ
  D_FF_AS d_ff_as_2 (.Set(1'b0), .D(or_3_out), .C(CLK), .Clr(CLR), .Q(d_ff_as_2_q));  // open: nQ
  D_FF_AS d_ff_as_3 (.Set(1'b0), .D(or_4_out), .C(CLK), .Clr(CLR), .Q(d_ff_as_3_q));  // open: nQ
  D_FF_AS d_ff_as_4 (.Set(1'b0), .D(or_5_out), .C(CLK), .Clr(CLR), .Q(d_ff_as_4_q));  // open: nQ
  D_FF_AS d_ff_as_5 (.Set(1'b0), .D(or_6_out), .C(CLK), .Clr(CLR), .Q(d_ff_as_5_q));  // open: nQ
  D_FF_AS d_ff_as_6 (.Set(1'b0), .D(or_7_out), .C(CLK), .Clr(CLR), .Q(d_ff_as_6_q));  // open: nQ
  D_FF_AS d_ff_as_7 (.Set(1'b0), .D(or_8_out), .C(CLK), .Clr(CLR), .Q(d_ff_as_7_q));  // open: nQ
  D_FF_AS d_ff_as_8 (.Set(1'b0), .D(or_9_out), .C(CLK), .Clr(CLR), .Q(d_ff_as_8_q));  // open: nQ
  D_FF_AS d_ff_as_9 (.Set(1'b0), .D(or_10_out), .C(CLK), .Clr(CLR), .Q(d_ff_as_9_q));  // open: nQ
  D_FF_AS d_ff_as_10 (.Set(1'b0), .D(or_11_out), .C(CLK), .Clr(CLR), .Q(d_ff_as_10_q));  // open: nQ
  D_FF_AS d_ff_as_11 (.Set(1'b0), .D(or_12_out), .C(CLK), .Clr(CLR), .Q(d_ff_as_11_q));  // open: nQ
  D_FF_AS d_ff_as_12 (.Set(1'b0), .D(or_13_out), .C(CLK), .Clr(CLR), .Q(d_ff_as_12_q));  // open: nQ
  D_FF_AS d_ff_as_13 (.Set(1'b0), .D(or_14_out), .C(CLK), .Clr(CLR), .Q(d_ff_as_13_q));  // open: nQ
  D_FF_AS d_ff_as_14 (.Set(1'b0), .D(or_15_out), .C(CLK), .Clr(CLR), .Q(d_ff_as_14_q));  // open: nQ
  D_FF_AS d_ff_as_15 (.Set(1'b0), .D(or_16_out), .C(CLK), .Clr(CLR), .Q(d_ff_as_15_q));  // open: nQ
  D_FF_AS d_ff_as_16 (.Set(1'b0), .D(or_17_out), .C(CLK), .Clr(CLR), .Q(d_ff_as_16_q));  // open: nQ
  assign Q0 = nor_1_out ? d_ff_as_1_q : 1'bz;  // Driver driver_1
  assign Q1 = nor_1_out ? d_ff_as_2_q : 1'bz;  // Driver driver_2
  assign Q2 = nor_1_out ? d_ff_as_3_q : 1'bz;  // Driver driver_3
  assign Q3 = nor_1_out ? d_ff_as_4_q : 1'bz;  // Driver driver_4
  assign Q4 = nor_1_out ? d_ff_as_5_q : 1'bz;  // Driver driver_5
  assign Q5 = nor_1_out ? d_ff_as_6_q : 1'bz;  // Driver driver_6
  assign Q6 = nor_1_out ? d_ff_as_7_q : 1'bz;  // Driver driver_7
  assign Q7 = nor_1_out ? d_ff_as_8_q : 1'bz;  // Driver driver_8
  assign Q8 = nor_1_out ? d_ff_as_9_q : 1'bz;  // Driver driver_9
  assign Q9 = nor_1_out ? d_ff_as_10_q : 1'bz;  // Driver driver_10
  assign Q10 = nor_1_out ? d_ff_as_11_q : 1'bz;  // Driver driver_11
  assign Q11 = nor_1_out ? d_ff_as_12_q : 1'bz;  // Driver driver_12
  assign Q12 = nor_1_out ? d_ff_as_13_q : 1'bz;  // Driver driver_13
  assign Q13 = nor_1_out ? d_ff_as_14_q : 1'bz;  // Driver driver_14
  assign Q14 = nor_1_out ? d_ff_as_15_q : 1'bz;  // Driver driver_15
  assign Q15 = nor_1_out ? d_ff_as_16_q : 1'bz;  // Driver driver_16

  // Notes on the sheet:
  //   CLR: default 1
  //   nL: pin 9
endmodule
