// Digital circuit d flipflop 8 bit.dig as structural Verilog
module d_flipflop_8_bit (
  input  CLR,
  input  CLK,
  input  nL,
  input  nOE,
  input  D0,
  input  D1,
  input  D2,
  input  D3,
  input  D4,
  input  D5,
  input  D6,
  input  D7,
  output Q0,
  output Q1,
  output Q2,
  output Q3,
  output Q4,
  output Q5,
  output Q6,
  output Q7
);

  wire and_1_out, and_2_out, and_3_out, and_4_out, and_5_out, and_6_out, and_7_out, and_8_out, and_9_out,
       and_10_out, and_11_out, and_12_out, and_13_out, and_14_out, and_15_out, and_16_out, d_ff_as_1_q,
       d_ff_as_2_q, d_ff_as_3_q, d_ff_as_4_q, d_ff_as_5_q, d_ff_as_6_q, d_ff_as_7_q, d_ff_as_8_q, nor_1_out,
       not_1_out, or_1_out, or_2_out, or_3_out, or_4_out, or_5_out, or_6_out, or_7_out, or_8_out, or_9_out;

  or or_1 (or_1_out, nL, nL);
  nor nor_1 (nor_1_out, nOE, nOE);
  not not_1 (not_1_out, or_1_out);
  and and_1 (and_1_out, d_ff_as_1_q, or_1_out);
  and and_2 (and_2_out, D0, not_1_out);
  and and_3 (and_3_out, d_ff_as_2_q, or_1_out);
  and and_4 (and_4_out, D1, not_1_out);
  and and_5 (and_5_out, d_ff_as_3_q, or_1_out);
  and and_6 (and_6_out, D2, not_1_out);
  and and_7 (and_7_out, d_ff_as_4_q, or_1_out);
  and and_8 (and_8_out, D3, not_1_out);
  and and_9 (and_9_out, d_ff_as_5_q, or_1_out);
  and and_10 (and_10_out, D4, not_1_out);
  and and_11 (and_11_out, d_ff_as_6_q, or_1_out);
  and and_12 (and_12_out, D5, not_1_out);
  and and_13 (and_13_out, d_ff_as_7_q, or_1_out);
  and and_14 (and_14_out, D6, not_1_out);
  and and_15 (and_15_out, d_ff_as_8_q, or_1_out);
  and and_16 (and_16_out, D7, not_1_out);
  or or_2 (or_2_out, and_1_out, and_2_out);
  or or_3 (or_3_out, and_3_out, and_4_out);
  or or_4 (or_4_out, and_5_out, and_6_out);
  or or_5 (or_5_out, and_7_out, and_8_out);
  or or_6 (or_6_out, and_9_out, and_10_out);
  or or_7 (or_7_out, and_11_out, and_12_out);
  or or_8 (or_8_out, and_13_out, and_14_out);
  or or_9 (or_9_out, and_15_out, and_16_out);
  D_FF_AS d_ff_as_1 (.Set(1'b0), .D(or_2_out), .C(CLK), .Clr(CLR), .Q(d_ff_as_1_q));  // open: nQ
  D_FF_AS d_ff_as_2 (.Set(1'b0), .D(or_3_out), .C(CLK), .Clr(CLR), .Q(d_ff_as_2_q));  // open: nQ
  D_FF_AS d_ff_as_3 (.Set(1'b0), .D(or_4_out), .C(CLK), .Clr(CLR), .Q(d_ff_as_3_q));  // open: nQ
  D_FF_AS d_ff_as_4 (.Set(1'b0), .D(or_5_out), .C(CLK), .Clr(CLR), .Q(d_ff_as_4_q));  // open: nQ
  D_FF_AS d_ff_as_5 (.Set(1'b0), .D(or_6_out), .C(CLK), .Clr(CLR), .Q(d_ff_as_5_q));  // open: nQ
  D_FF_AS d_ff_as_6 (.Set(1'b0), .D(or_7_out), .C(CLK), .Clr(CLR), .Q(d_ff_as_6_q));  // open: nQ
  D_FF_AS d_ff_as_7 (.Set(1'b0), .D(or_8_out), .C(CLK), .Clr(CLR), .Q(d_ff_as_7_q));  // open: nQ
  D_FF_AS d_ff_as_8 (.Set(1'b0), .D(or_9_out), .C(CLK), .Clr(CLR), .Q(d_ff_as_8_q));  // open: nQ
  assign Q0 = nor_1_out ? d_ff_as_1_q : 1'bz;  // Driver driver_1
  assign Q1 = nor_1_out ? d_ff_as_2_q : 1'bz;  // Driver driver_2
  assign Q2 = nor_1_out ? d_ff_as_3_q : 1'bz;  // Driver driver_3
  assign Q3 = nor_1_out ? d_ff_as_4_q : 1'bz;  // Driver driver_4
  assign Q4 = nor_1_out ? d_ff_as_5_q : 1'bz;  // Driver driver_5
  assign Q5 = nor_1_out ? d_ff_as_6_q : 1'bz;  // Driver driver_6
  assign Q6 = nor_1_out ? d_ff_as_7_q : 1'bz;  // Driver driver_7
  assign Q7 = nor_1_out ? d_ff_as_8_q : 1'bz;  // Driver driver_8

  // Notes on the sheet:
  //   CLR: default 1
  //   nL: pin 9
endmodule
