// Digital circuit d flipflop w probe.dig as structural Verilog
module d_flipflop_w_probe (
  input  CLR,
  input  CLK,
  input  nL,
  input  nOE,
  input  [7:0] D,
  output [7:0] Q,
  output [7:0] Qp
);

  wire and_1_out, and_2_out, and_3_out, and_4_out, and_5_out, and_6_out, and_7_out, and_8_out, and_9_out,
       and_10_out, and_11_out, and_12_out, and_13_out, and_14_out, and_15_out, and_16_out, nor_1_out,
       not_1_out, or_1_out, or_2_out, or_3_out, or_4_out, or_5_out, or_6_out, or_7_out, or_8_out, or_9_out;

  or or_1 (or_1_out, nL, nL);
  nor nor_1 (nor_1_out, nOE, nOE);
  not not_1 (not_1_out, or_1_out);
  and and_1 (and_1_out, Qp[0], or_1_out);
  and and_2 (and_2_out, D[0], not_1_out);
  and and_3 (and_3_out, Q[0], or_1_out);
  and and_4 (and_4_out, D[1], not_1_out);
  and and_5 (and_5_out, Qp[2], or_1_out);
  and and_6 (and_6_out, D[2], not_1_out);
  and and_7 (and_7_out, Qp[3], or_1_out);
  and and_8 (and_8_out, D[3], not_1_out);
  and and_9 (and_9_out, Qp[4], or_1_out);
  and and_10 (and_10_out, D[4], not_1_out);
  and and_11 (and_11_out, Qp[5], or_1_out);
  and and_12 (and_12_out, D[5], not_1_out);
  and and_13 (and_13_out, Qp[6], or_1_out);
  and and_14 (and_14_out, D[6], not_1_out);
  and and_15 (and_15_out, Qp[7], or_1_out);
  and and_16 (and_16_out, D[7], not_1_out);
  or or_2 (or_2_out, and_1_out, and_2_out);
  or or_3 (or_3_out, and_3_out, and_4_out);
  or or_4 (or_4_out, and_5_out, and_6_out);
  or or_5 (or_5_out, and_7_out, and_8_out);
  or or_6 (or_6_out, and_9_out, and_10_out);
  or or_7 (or_7_out, and_11_out, and_12_out);
  or or_8 (or_8_out, and_13_out, and_14_out);
  or or_9 (or_9_out, and_15_out, and_16_out);
  D_FF_AS d_ff_as_1 (.Set(1'b0), .D(or_2_out), .C(CLK), .Clr(CLR), .Q(Qp[0]));  // open: nQ
  D_FF_AS d_ff_as_2 (.Set(1'b0), .D(or_3_out), .C(CLK), .Clr(CLR), .Q(Q[0]));  // open: nQ
  D_FF_AS d_ff_as_3 (.Set(1'b0), .D(or_4_out), .C(CLK), .Clr(CLR), .Q(Qp[2]));  // open: nQ
  D_FF_AS d_ff_as_4 (.Set(1'b0), .D(or_5_out), .C(CLK), .Clr(CLR), .Q(Qp[3]));  // open: nQ
  D_FF_AS d_ff_as_5 (.Set(1'b0), .D(or_6_out), .C(CLK), .Clr(CLR), .Q(Qp[4]));  // open: nQ
  D_FF_AS d_ff_as_6 (.Set(1'b0), .D(or_7_out), .C(CLK), .Clr(CLR), .Q(Qp[5]));  // open: nQ
  D_FF_AS d_ff_as_7 (.Set(1'b0), .D(or_8_out), .C(CLK), .Clr(CLR), .Q(Qp[6]));  // open: nQ
  D_FF_AS d_ff_as_8 (.Set(1'b0), .D(or_9_out), .C(CLK), .Clr(CLR), .Q(Qp[7]));  // open: nQ
  assign Q[0] = nor_1_out ? Qp[0] : 1'bz;  // Driver driver_1
  assign Q[1] = nor_1_out ? Q[0] : 1'bz;  // Driver driver_2
  assign Q[2] = nor_1_out ? Qp[2] : 1'bz;  // Driver driver_3
  assign Q[3] = nor_1_out ? Qp[3] : 1'bz;  // Driver driver_4
  assign Q[4] = nor_1_out ? Qp[4] : 1'bz;  // Driver driver_5
  assign Q[5] = nor_1_out ? Qp[5] : 1'bz;  // Driver driver_6
  assign Q[6] = nor_1_out ? Qp[6] : 1'bz;  // Driver driver_7
  assign Q[7] = nor_1_out ? Qp[7] : 1'bz;  // Driver driver_8

  assign Qp[1] = Q[0];

  // Other names for the same wires on the sheet: b0 = Qp[0]; b1 = Q[0]; b2 = Qp[2]; b3 = Qp[3]; b4 = Qp[4];
  //   b5 = Qp[5]; b6 = Qp[6]; b7 = Qp[7]

  // Notes on the sheet:
  //   CLR: default 1
  //   nL: pin 9
endmodule
